// Digital circuit Lojik odev.dig as structural Verilog
module Lojik_odev (
  input  in_1,
  input  in_2,
  input  in_3,
  input  in_4,
  input  in_5,
  input  in_6,
  input  in_7,
  input  in_8,
  input  in_9,
  input  in_10,
  input  in_11,
  output out_12,
  output out_13,
  output out_14,
  output out_15,
  output out_16
);

  wire add_1_c_o, add_1_s, add_2_c_o, add_2_s, add_3_c_o, add_3_s, add_4_s, and_1_out, and_2_out, and_3_out,
       and_4_out, and_5_out, and_6_out, and_7_out, and_8_out, and_9_out, and_10_out, and_11_out, and_12_out,
       and_13_out, and_14_out, and_15_out, demultiplexer_1_out_1, demultiplexer_1_out_2,
       demultiplexer_1_out_3, demultiplexer_2_out_0, demultiplexer_2_out_1, demultiplexer_2_out_2,
       demultiplexer_2_out_3, demultiplexer_3_out_1, demultiplexer_3_out_2, demultiplexer_3_out_3,
       demultiplexer_4_out_0, demultiplexer_4_out_1, demultiplexer_4_out_2, demultiplexer_4_out_3,
       demultiplexer_5_out_1, demultiplexer_5_out_2, demultiplexer_5_out_3, demultiplexer_6_out_0,
       demultiplexer_6_out_1, demultiplexer_6_out_2, demultiplexer_6_out_3, demultiplexer_7_out_1,
       demultiplexer_7_out_2, demultiplexer_7_out_3, demultiplexer_8_out_0, demultiplexer_8_out_1,
       demultiplexer_8_out_2, demultiplexer_8_out_3, not_1_out, not_2_out, not_3_out, not_4_out, not_5_out,
       not_6_out, not_7_out, not_8_out, or_1_out, or_2_out, or_3_out, or_4_out, or_5_out, xor_1_out,
       xor_2_out, xor_3_out, xor_4_out, xor_5_out, xor_6_out, xor_7_out, xor_8_out;
  wire [2:0] not_11_out;

  not not_1 (not_1_out, in_3);
  and and_1 (and_1_out, in_8, not_1_out);
  and and_2 (and_2_out, in_9, not_1_out);
  and and_3 (and_3_out, in_10, not_1_out);
  and and_4 (and_4_out, in_11, not_1_out);
  and and_5 (and_5_out, in_4, not_1_out);
  and and_6 (and_6_out, in_5, not_1_out);
  and and_7 (and_7_out, in_6, not_1_out);
  and and_8 (and_8_out, in_7, not_1_out);
  Demultiplexer #(.Selector_Bits(2)) demultiplexer_1 (
    .sel({in_2, in_1}), .in(in_11), .out_1(demultiplexer_1_out_1), .out_2(demultiplexer_1_out_2),
    .out_3(demultiplexer_1_out_3));  // open: out_0
  Demultiplexer #(.Selector_Bits(2)) demultiplexer_2 (
    .sel({in_2, in_1}), .in(in_7), .out_0(demultiplexer_2_out_0), .out_1(demultiplexer_2_out_1),
    .out_2(demultiplexer_2_out_2), .out_3(demultiplexer_2_out_3));
  Demultiplexer #(.Selector_Bits(2)) demultiplexer_3 (
    .sel({in_2, in_1}), .in(in_10), .out_1(demultiplexer_3_out_1), .out_2(demultiplexer_3_out_2),
    .out_3(demultiplexer_3_out_3));  // open: out_0
  Demultiplexer #(.Selector_Bits(2)) demultiplexer_4 (
    .sel({in_2, in_1}), .in(in_6), .out_0(demultiplexer_4_out_0), .out_1(demultiplexer_4_out_1),
    .out_2(demultiplexer_4_out_2), .out_3(demultiplexer_4_out_3));
  Demultiplexer #(.Selector_Bits(2)) demultiplexer_5 (
    .sel({in_2, in_1}), .in(in_9), .out_1(demultiplexer_5_out_1), .out_2(demultiplexer_5_out_2),
    .out_3(demultiplexer_5_out_3));  // open: out_0
  Demultiplexer #(.Selector_Bits(2)) demultiplexer_6 (
    .sel({in_2, in_1}), .in(in_5), .out_0(demultiplexer_6_out_0), .out_1(demultiplexer_6_out_1),
    .out_2(demultiplexer_6_out_2), .out_3(demultiplexer_6_out_3));
  Demultiplexer #(.Selector_Bits(2)) demultiplexer_7 (
    .sel({in_2, in_1}), .in(in_8), .out_1(demultiplexer_7_out_1), .out_2(demultiplexer_7_out_2),
    .out_3(demultiplexer_7_out_3));  // open: out_0
  Demultiplexer #(.Selector_Bits(2)) demultiplexer_8 (
    .sel({in_2, in_1}), .in(in_4), .out_0(demultiplexer_8_out_0), .out_1(demultiplexer_8_out_1),
    .out_2(demultiplexer_8_out_2), .out_3(demultiplexer_8_out_3));
  not not_2 (not_2_out, demultiplexer_2_out_0);
  not not_3 (not_3_out, demultiplexer_4_out_0);
  not not_4 (not_4_out, demultiplexer_6_out_0);
  not not_5 (not_5_out, demultiplexer_8_out_0);
  not not_6 (not_6_out, in_2);
  not not_7 (not_7_out, in_2);
  not not_8 (not_8_out, in_2);
  and and_9 (and_9_out, demultiplexer_1_out_2, demultiplexer_2_out_2);
  or or_1 (or_1_out, demultiplexer_1_out_1, demultiplexer_2_out_1);
  and and_10 (and_10_out, demultiplexer_3_out_2, demultiplexer_4_out_2);
  or or_2 (or_2_out, demultiplexer_3_out_1, demultiplexer_4_out_1);
  and and_11 (and_11_out, demultiplexer_5_out_2, demultiplexer_6_out_2);
  or or_3 (or_3_out, demultiplexer_5_out_1, demultiplexer_6_out_1);
  and and_12 (and_12_out, demultiplexer_7_out_2, demultiplexer_8_out_2);
  or or_4 (or_4_out, demultiplexer_7_out_1, demultiplexer_8_out_1);
  or or_5 (or_5_out, and_1_out, in_2);
  and and_13 (and_13_out, and_2_out, not_6_out);
  and and_14 (and_14_out, and_3_out, not_7_out);
  and and_15 (and_15_out, and_4_out, not_8_out);
  xor xor_1 (xor_1_out, demultiplexer_1_out_3, demultiplexer_2_out_3);
  xor xor_2 (xor_2_out, demultiplexer_3_out_3, demultiplexer_4_out_3);
  xor xor_3 (xor_3_out, demultiplexer_5_out_3, demultiplexer_6_out_3);
  xor xor_4 (xor_4_out, demultiplexer_7_out_3, demultiplexer_8_out_3);
  xor xor_5 (xor_5_out, or_5_out, in_1);
  xor xor_6 (xor_6_out, and_13_out, in_1);
  xor xor_7 (xor_7_out, and_14_out, in_1);
  xor xor_8 (xor_8_out, and_15_out, in_1);
  not not_9 (not_11_out[0], in_1);
  not not_10 (not_11_out[1], in_2);
  not not_11 (not_11_out[2], in_3);
  Add add_1 (.a(and_5_out), .b(xor_5_out), .c_i(in_1), .s(add_1_s), .c_o(add_1_c_o));
  Add add_2 (.a(and_6_out), .b(xor_6_out), .c_i(add_1_c_o), .s(add_2_s), .c_o(add_2_c_o));
  Add add_3 (.a(and_7_out), .b(xor_7_out), .c_i(add_2_c_o), .s(add_3_s), .c_o(add_3_c_o));
  Add add_4 (.a(and_8_out), .b(xor_8_out), .c_i(add_3_c_o), .s(add_4_s), .c_o(out_16));
  Multiplexer #(.Selector_Bits(3)) multiplexer_1 (
    .sel(not_11_out), .in_0(xor_2_out), .in_1(and_10_out), .in_2(or_2_out), .in_3(not_3_out), .in_4(add_3_s),
    .in_5(add_3_s), .in_6(add_3_s), .in_7(add_3_s), .out(out_14));
  Multiplexer #(.Selector_Bits(3)) multiplexer_2 (
    .sel(not_11_out), .in_0(xor_3_out), .in_1(and_11_out), .in_2(or_3_out), .in_3(not_4_out), .in_4(add_2_s),
    .in_5(add_2_s), .in_6(add_2_s), .in_7(add_2_s), .out(out_13));
  Multiplexer #(.Selector_Bits(3)) multiplexer_3 (
    .sel(not_11_out), .in_0(xor_1_out), .in_1(and_9_out), .in_2(or_1_out), .in_3(not_2_out), .in_4(add_4_s),
    .in_5(add_4_s), .in_6(add_4_s), .in_7(add_4_s), .out(out_15));
  Multiplexer #(.Selector_Bits(3)) multiplexer_4 (
    .sel(not_11_out), .in_0(xor_4_out), .in_1(and_12_out), .in_2(or_4_out), .in_3(not_5_out), .in_4(add_1_s),
    .in_5(add_1_s), .in_6(add_1_s), .in_7(add_1_s), .out(out_12));

  // Notes on the sheet:
  //   F0
  //   F1
  //   F2
  //   A0
  //   A1
  //   A2
  //   A3
  //   B0
  //   B1
  //   B2
  //   B3
  //   Carry
  //   Output
  //   0
  //   1
  //   2
  //   3
endmodule
