// Digital circuit lojikodev_1_1.dig as structural Verilog
module lojikodev_1_1 (
  input  B3,
  input  A3,
  input  B2,
  input  A2,
  input  B1,
  input  A1,
  input  B0,
  input  A0,
  input  M
);

  wire add_1_c_o, add_1_s, add_2_c_o, add_2_s, add_3_c_o, add_3_s, add_4_c_o, add_4_s, xor_1_out, xor_2_out,
       xor_3_out, xor_4_out;

  LED F4 (.in(add_1_c_o));
  xor xor_1 (xor_1_out, B3, M);
  Add add_1 (.a(A3), .b(xor_1_out), .c_i(add_2_c_o), .s(add_1_s), .c_o(add_1_c_o));
  LED F3 (.in(add_1_s));
  xor xor_2 (xor_2_out, B2, M);
  Add add_2 (.a(A2), .b(xor_2_out), .c_i(add_3_c_o), .s(add_2_s), .c_o(add_2_c_o));
  LED F2 (.in(add_2_s));
  xor xor_3 (xor_3_out, B1, M);
  Add add_3 (.a(A1), .b(xor_3_out), .c_i(add_4_c_o), .s(add_3_s), .c_o(add_3_c_o));
  LED F1 (.in(add_3_s));
  xor xor_4 (xor_4_out, B0, M);
  Add add_4 (.a(A0), .b(xor_4_out), .c_i(M), .s(add_4_s), .c_o(add_4_c_o));
  LED F0 (.in(add_4_s));
endmodule
