// Digital circuit devre_1.dig as structural Verilog
module devre_1 (
  input  X,
  input  CLK
);

  wire and_1_out, and_2_out, jk_ff_1_q, jk_ff_2_q, not_1_out, not_2_out, not_3_out, not_4_out, or_1_out;

  not not_1 (not_1_out, X);
  not not_2 (not_2_out, X);
  not not_3 (not_3_out, X);
  not not_4 (not_4_out, X);
  and and_1 (and_1_out, not_1_out, jk_ff_2_q);
  or or_1 (or_1_out, not_2_out, jk_ff_2_q);
  JK_FF jk_ff_1 (.J(and_1_out), .C(CLK), .K(or_1_out), .Q(jk_ff_1_q));  // open: nQ
  JK_FF jk_ff_2 (.J(X), .C(CLK), .K(not_4_out), .Q(jk_ff_2_q));  // open: nQ
  and and_2 (and_2_out, jk_ff_1_q, not_3_out, jk_ff_2_q);
  LED led_1 (.in(and_2_out));
endmodule
