// Digital circuit devre_2.dig as structural Verilog
module devre_2 (
  input  X,
  input  CLK
);

  wire and_1_out, and_2_out, and_3_out, and_4_out, jk_ff_1_q, jk_ff_2_q, jk_ff_3_q;

  and and_1 (and_1_out, X, jk_ff_3_q, jk_ff_2_q);
  and and_2 (and_2_out, X, jk_ff_3_q, jk_ff_2_q);
  and and_3 (and_3_out, X, jk_ff_3_q);
  and and_4 (and_4_out, X, jk_ff_3_q);
  JK_FF jk_ff_1 (.J(and_1_out), .C(CLK), .K(and_2_out), .Q(jk_ff_1_q));  // open: nQ
  JK_FF jk_ff_2 (.J(and_3_out), .C(CLK), .K(and_4_out), .Q(jk_ff_2_q));  // open: nQ
  JK_FF jk_ff_3 (.J(X), .C(CLK), .K(X), .Q(jk_ff_3_q));  // open: nQ
  LED led_1 (.in(jk_ff_1_q));
  LED led_2 (.in(jk_ff_2_q));
  LED led_3 (.in(jk_ff_3_q));
endmodule
