// Digital circuit Homework1.dig as structural Verilog
module Homework1 (
  input  D1,
  input  D2,
  input  D3,
  input  D4,
  input  Sub1,
  input  Sub2,
  input  Sub3,
  input  Sub4,
  input  M1,
  input  M2,
  input  En,
  input  clk
);

  wire and_3_out, and_4_out, and_5_out, and_6_out, and_7_out, and_8_out, and_9_out, and_10_out,
       dipswitch_1_out, dipswitch_2_out, dipswitch_3_out, dipswitch_4_out, dipswitch_5_out, dipswitch_6_out,
       EnAndM1, EnAndM2, m1_t, m2_t, m3, m4, Mux1Out, Mux2Out, Mux3Out, Mux4Out, not_1_out, not_2_out,
       not_3_out, not_4_out, Q1, Q1_t, Q2, Q2_t, Q3, Q3_t, Q4, Q4_t, Sub1_t, Sub2_t, Sub3_t, Sub4_t, Sum1,
       Sum2, Sum3, Sum4, xor_1_out, xor_2_out, xor_3_out, xor_4_out;

  // Probe on M2
  // Probe on M1
  // Probe on En
  // Probe on En
  and and_1 (EnAndM2, En, M2);
  // Probe on En
  and and_2 (EnAndM1, En, M1);
  // Probe on D1
  // Probe on D2
  // Probe on D3
  // Probe on D4
  // Probe on EnAndM2
  // Probe on EnAndM1
  // Probe on M1
  // Probe on M2
  // Probe on EnAndM2
  // Probe on EnAndM2
  // Probe on EnAndM2
  // Probe on EnAndM2
  // Probe on EnAndM1
  // Probe on EnAndM1
  // Probe on EnAndM1
  // Probe on EnAndM1
  Multiplexer #(.Selector_Bits(2)) multiplexer_1 (
    .sel({EnAndM2, EnAndM1}), .in_0(m1_t), .in_1(Sum1), .in_2(D1), .in_3(Sub1), .out(Mux1Out));
  Multiplexer #(.Selector_Bits(2)) multiplexer_2 (
    .sel({EnAndM2, EnAndM1}), .in_0(m2_t), .in_1(Sum2), .in_2(D2), .in_3(Sub2), .out(Mux2Out));
  Multiplexer #(.Selector_Bits(2)) multiplexer_3 (
    .sel({EnAndM2, EnAndM1}), .in_0(m3), .in_1(Sum3), .in_2(D3), .in_3(Sub3), .out(Mux3Out));
  Multiplexer #(.Selector_Bits(2)) multiplexer_4 (
    .sel({EnAndM2, EnAndM1}), .in_0(m4), .in_1(Sum4), .in_2(D4), .in_3(Sub4), .out(Mux4Out));
  // Probe on Mux1Out
  LED led_1 (.in(Mux1Out));
  // Probe on Mux2Out
  LED led_2 (.in(Mux2Out));
  // Probe on Mux3Out
  LED led_3 (.in(Mux3Out));
  // Probe on Mux4Out
  LED led_4 (.in(Mux4Out));
  DipSwitch #(.dipDefault("true")) dipswitch_1 (.out(dipswitch_1_out));
  DipSwitch #(.dipDefault("true")) dipswitch_2 (.out(dipswitch_2_out));
  DipSwitch #(.dipDefault("true")) dipswitch_3 (.out(dipswitch_3_out));
  DipSwitch #(.dipDefault("true")) dipswitch_4 (.out(dipswitch_4_out));
  xor xor_1 (xor_1_out, Mux1Out, dipswitch_1_out);
  xor xor_2 (xor_2_out, Mux2Out, dipswitch_2_out);
  xor xor_3 (xor_3_out, Mux3Out, dipswitch_3_out);
  xor xor_4 (xor_4_out, Mux4Out, dipswitch_4_out);
  JK_FF jk_ff_1 (.J(Mux1Out), .C(clk), .K(xor_1_out), .Q(Q1), .nQ(Q1_t));
  JK_FF jk_ff_2 (.J(Mux2Out), .C(clk), .K(xor_2_out), .Q(Q2), .nQ(Q2_t));
  JK_FF jk_ff_3 (.J(Mux3Out), .C(clk), .K(xor_3_out), .Q(Q3), .nQ(Q3_t));
  JK_FF jk_ff_4 (.J(Mux4Out), .C(clk), .K(xor_4_out), .Q(Q4), .nQ(Q4_t));
  LED led_5 (.in(Q1));
  LED led_6 (.in(Q1_t));
  LED led_7 (.in(Q2));
  LED led_8 (.in(Q2_t));
  LED led_9 (.in(Q3));
  LED led_10 (.in(Q3_t));
  LED led_11 (.in(Q4));
  LED led_12 (.in(Q4_t));
  // Probe on Q1
  // Probe on Q1_t
  // Probe on Q2
  // Probe on Q2_t
  // Probe on Q3
  // Probe on Q3_t
  // Probe on Q4
  // Probe on Q4_t
  // Probe on En
  // Probe on Q1
  // Probe on En
  // Probe on Q2
  // Probe on En
  // Probe on Q3
  // Probe on En
  // Probe on Q4
  xor xor_5 (m1_t, En, Q1);
  xor xor_6 (m2_t, En, Q2);
  xor xor_7 (m3, En, Q3);
  xor xor_8 (m4, En, Q4);
  LED led_13 (.in(m1_t));
  // Probe on m1_t
  LED led_14 (.in(m2_t));
  // Probe on m2_t
  LED led_15 (.in(m3));
  // Probe on m3
  LED led_16 (.in(m4));
  // Probe on m4
  DipSwitch #(.dipDefault("true")) dipswitch_5 (.out(dipswitch_5_out));
  // Probe on Q1_t
  // Probe on dipswitch_5_out
  // Probe on and_5_out
  // Probe on Q3_t
  xor xor_9 (Sum1, Q1_t, dipswitch_5_out);
  and and_3 (and_3_out, dipswitch_5_out, Q1_t);
  xor xor_10 (Sum3, and_5_out, Q3_t);
  and and_4 (and_4_out, Q3_t, and_5_out);
  // Probe on Sum1
  LED Sum (.in(Sum1));
  // Probe on and_3_out
  LED Cout (.in(and_3_out));
  // Probe on Sum3
  LED Sum_2 (.in(Sum3));
  // Probe on and_4_out
  LED Cout_2 (.in(and_4_out));
  // Probe on and_3_out
  // Probe on and_4_out
  // Probe on Q2_t
  // Probe on Q4_t
  xor xor_11 (Sum2, and_3_out, Q2_t);
  and and_5 (and_5_out, Q2_t, and_3_out);
  xor xor_12 (Sum4, and_4_out, Q4_t);
  and and_6 (and_6_out, Q4_t, and_4_out);
  // Probe on Sum2
  LED Sum_3 (.in(Sum2));
  // Probe on and_5_out
  LED Cout_3 (.in(and_5_out));
  // Probe on Sum4
  LED Sum_4 (.in(Sum4));
  // Probe on and_6_out
  LED Cout_4 (.in(and_6_out));
  DipSwitch #(.dipDefault("true")) dipswitch_6 (.out(dipswitch_6_out));
  // Probe on Q3
  not not_1 (not_1_out, Q3);
  // Probe on Q1
  // Probe on dipswitch_6_out
  not not_2 (not_2_out, Q1);
  // Probe on and_10_out
  xor xor_13 (Sub1_t, Q1, dipswitch_6_out);
  and and_7 (and_7_out, dipswitch_6_out, not_2_out);
  xor xor_14 (Sub3_t, Q3, and_10_out);
  and and_8 (and_8_out, and_10_out, not_1_out);
  // Probe on Q2
  // Probe on Sub3_t
  // Probe on and_8_out
  // Probe on Q4
  not not_3 (not_3_out, Q4);
  // Probe on Sub1_t
  LED Difference (.in(Sub1_t));
  // Probe on and_7_out
  LED Borrow (.in(and_7_out));
  // Probe on and_7_out
  not not_4 (not_4_out, Q2);
  LED Difference_2 (.in(Sub3_t));
  LED Borrow_2 (.in(and_8_out));
  // Probe on and_8_out
  xor xor_15 (Sub4_t, Q4, and_8_out);
  and and_9 (and_9_out, and_8_out, not_3_out);
  xor xor_16 (Sub2_t, Q2, and_7_out);
  and and_10 (and_10_out, and_7_out, not_4_out);
  // Probe on Sub4_t
  // Probe on and_9_out
  // Probe on Sub2_t
  LED Difference_3 (.in(Sub2_t));
  // Probe on and_10_out
  LED Borrow_3 (.in(and_10_out));
  LED Difference_4 (.in(Sub4_t));
  LED Borrow_4 (.in(and_9_out));
endmodule
