// Digital circuit IntermediateCircuit_1.dig as structural Verilog
module IntermediateCircuit_1 (
  input  M1,
  input  M2,
  input  En,
  input  clk,
  input  M3,
  input  M4,
  input  En_2,
  input  clk_2
);

  wire and_1_out, and_2_out, EnAndM1, EnAndM2, m1_t, m2_t, m3_t, m4_t, Q1, Q1_t, Q2, Q2_t, Q3, Q3_t, Q4, Q4_t;

  // Probe on M2
  // Probe on M1
  // Probe on En
  // Probe on En
  and and_1 (and_1_out, En, M2);
  // Probe on En
  and and_2 (and_2_out, En, M1);
  // Probe on En
  // Probe on Q1
  xor xor_1 (m1_t, En, Q1);
  JK_FF jk_ff_1 (.J(and_1_out), .C(clk), .K(and_2_out), .Q(Q1), .nQ(Q1_t));
  LED led_1 (.in(m1_t));
  // Probe on M1
  // Probe on M2
  // Probe on m1_t
  // Probe on Q1
  LED led_2 (.in(Q1));
  LED led_3 (.in(Q1_t));
  // Probe on Q1_t
  // Probe on En
  // Probe on M2
  // Probe on M1
  // Probe on En
  // Probe on En
  and and_3 (EnAndM2, En, M2);
  and and_4 (EnAndM1, En, M1);
  // Probe on EnAndM2
  // Probe on EnAndM1
  // Probe on M1
  // Probe on M2
  JK_FF jk_ff_2 (.J(EnAndM2), .C(clk_2), .K(EnAndM1), .Q(Q1), .nQ(Q1_t));
  JK_FF jk_ff_3 (.J(EnAndM2), .C(clk_2), .K(EnAndM1), .Q(Q2), .nQ(Q2_t));
  JK_FF jk_ff_4 (.J(EnAndM2), .C(clk_2), .K(EnAndM1), .Q(Q3), .nQ(Q3_t));
  JK_FF jk_ff_5 (.J(EnAndM2), .C(clk_2), .K(EnAndM1), .Q(Q4), .nQ(Q4_t));
  // Probe on Q1
  LED led_4 (.in(Q1));
  LED led_5 (.in(Q1_t));
  // Probe on Q1_t
  // Probe on Q2
  LED led_6 (.in(Q2));
  LED led_7 (.in(Q2_t));
  // Probe on Q2_t
  // Probe on Q3
  LED led_8 (.in(Q3));
  LED led_9 (.in(Q3_t));
  // Probe on Q3_t
  // Probe on Q4
  LED led_10 (.in(Q4));
  LED led_11 (.in(Q4_t));
  // Probe on Q4_t
  // Probe on En
  // Probe on Q1
  // Probe on En
  // Probe on Q2
  // Probe on En
  // Probe on Q3
  // Probe on En
  // Probe on Q4
  xor xor_2 (m1_t, En, Q1);
  xor xor_3 (m2_t, En, Q2);
  xor xor_4 (m3_t, En, Q3);
  xor xor_5 (m4_t, En, Q4);
  LED led_12 (.in(m1_t));
  // Probe on m1_t
  LED led_13 (.in(m2_t));
  // Probe on m2_t
  LED led_14 (.in(m3_t));
  // Probe on m3_t
  LED led_15 (.in(m4_t));
  // Probe on m4_t

  assign En_2 = En;
  assign M3 = M1;
  assign M4 = M2;

  // Other names for the same wires on the sheet: CLK_t = clk_2
endmodule
