// Digital circuit IntermediateCircuit_2.dig as structural Verilog
module IntermediateCircuit_2 (
  input  D1,
  input  D2,
  input  D3,
  input  D4,
  input  D9,
  input  D11,
  input  D12,
  input  D14,
  input  D15,
  input  D17,
  input  D18,
  input  D20,
  input  M1,
  input  M2,
  input  En,
  input  clk,
  input  A,
  input  B,
  input  A_2,
  input  B_2
);

  wire and_3_out, and_4_out, dipswitch_1_out, dipswitch_2_out, dipswitch_3_out, dipswitch_4_out, EnAndM1,
       EnAndM2, m1_t, m2_t, m3, m4, Mux1Out, Mux2Out, Mux3Out, Mux4Out, not_1_out, Q1, Q1_t, Q2, Q2_t, Q3,
       Q3_t, Q4, Q4_t, xor_1_out, xor_2_out, xor_3_out, xor_4_out, xor_9_out, xor_10_out;

  // Probe on M2
  // Probe on M1
  // Probe on En
  // Probe on En
  // Probe on En
  and and_1 (EnAndM2, En, M2);
  and and_2 (EnAndM1, En, M1);
  // Probe on D1
  // Probe on D2
  // Probe on D3
  // Probe on D4
  // Probe on EnAndM2
  // Probe on EnAndM1
  // Probe on M1
  // Probe on M2
  // Probe on EnAndM1
  // Probe on EnAndM2
  // Probe on EnAndM1
  // Probe on EnAndM2
  // Probe on EnAndM1
  // Probe on EnAndM2
  // Probe on EnAndM1
  // Probe on EnAndM2
  Multiplexer #(.Selector_Bits(2)) multiplexer_1 (
    .sel({EnAndM2, EnAndM1}), .in_0(m1_t), .in_1(D9), .in_2(D1), .in_3(D11), .out(Mux1Out));
  Multiplexer #(.Selector_Bits(2)) multiplexer_2 (
    .sel({EnAndM2, EnAndM1}), .in_0(m2_t), .in_1(D12), .in_2(D2), .in_3(D14), .out(Mux2Out));
  Multiplexer #(.Selector_Bits(2)) multiplexer_3 (
    .sel({EnAndM2, EnAndM1}), .in_0(m3), .in_1(D15), .in_2(D3), .in_3(D17), .out(Mux3Out));
  Multiplexer #(.Selector_Bits(2)) multiplexer_4 (
    .sel({EnAndM2, EnAndM1}), .in_0(m4), .in_1(D18), .in_2(D4), .in_3(D20), .out(Mux4Out));
  // Probe on Mux1Out
  LED led_1 (.in(Mux1Out));
  // Probe on Mux2Out
  LED led_2 (.in(Mux2Out));
  // Probe on Mux3Out
  LED led_3 (.in(Mux3Out));
  // Probe on Mux4Out
  LED led_4 (.in(Mux4Out));
  xor xor_1 (xor_1_out, Mux1Out, dipswitch_1_out);
  DipSwitch #(.dipDefault("true")) dipswitch_1 (.out(dipswitch_1_out));
  xor xor_2 (xor_2_out, Mux2Out, dipswitch_2_out);
  DipSwitch #(.dipDefault("true")) dipswitch_2 (.out(dipswitch_2_out));
  xor xor_3 (xor_3_out, Mux3Out, dipswitch_3_out);
  DipSwitch #(.dipDefault("true")) dipswitch_3 (.out(dipswitch_3_out));
  xor xor_4 (xor_4_out, Mux4Out, dipswitch_4_out);
  DipSwitch #(.dipDefault("true")) dipswitch_4 (.out(dipswitch_4_out));
  JK_FF jk_ff_1 (.J(Mux1Out), .C(clk), .K(xor_1_out), .Q(Q1), .nQ(Q1_t));
  JK_FF jk_ff_2 (.J(Mux2Out), .C(clk), .K(xor_2_out), .Q(Q2), .nQ(Q2_t));
  JK_FF jk_ff_3 (.J(Mux3Out), .C(clk), .K(xor_3_out), .Q(Q3), .nQ(Q3_t));
  JK_FF jk_ff_4 (.J(Mux4Out), .C(clk), .K(xor_4_out), .Q(Q4), .nQ(Q4_t));
  // Probe on Q1
  LED led_5 (.in(Q1));
  LED led_6 (.in(Q1_t));
  // Probe on Q1_t
  // Probe on Q2
  LED led_7 (.in(Q2));
  LED led_8 (.in(Q2_t));
  // Probe on Q2_t
  // Probe on Q3
  LED led_9 (.in(Q3));
  LED led_10 (.in(Q3_t));
  // Probe on Q3_t
  // Probe on Q4
  LED led_11 (.in(Q4));
  LED led_12 (.in(Q4_t));
  // Probe on Q4_t
  // Probe on En
  // Probe on Q1
  // Probe on En
  // Probe on Q2
  // Probe on En
  // Probe on Q3
  // Probe on En
  // Probe on Q4
  xor xor_5 (m1_t, En, Q1);
  xor xor_6 (m2_t, En, Q2);
  xor xor_7 (m3, En, Q3);
  xor xor_8 (m4, En, Q4);
  LED led_13 (.in(m1_t));
  // Probe on m1_t
  LED led_14 (.in(m2_t));
  // Probe on m2_t
  LED led_15 (.in(m3));
  // Probe on m3
  LED led_16 (.in(m4));
  // Probe on m4
  // Probe on A
  // Probe on A_2
  not not_1 (not_1_out, A_2);
  // Probe on B
  // Probe on B_2
  xor xor_9 (xor_9_out, A, B);
  and and_3 (and_3_out, B, A);
  xor xor_10 (xor_10_out, A_2, B_2);
  and and_4 (and_4_out, B_2, not_1_out);
  // Probe on xor_9_out
  // Probe on and_3_out
  // Probe on xor_10_out
  // Probe on and_4_out
  LED Sum (.in(xor_9_out));
  LED Cout (.in(and_3_out));
  LED Difference (.in(xor_10_out));
  LED Borrow (.in(and_4_out));
endmodule
